# Fritzing sketch ProjectSketchSchem (saved by Fritzing 0.9.3b)
breadboards: 1

parts:
  Part1 = Arduino Mega 2560 (Rev3)
  J1 = Basic Servo
  J2 = Infrared Proximity Sensor
  J3 = Infrared Proximity Sensor
  J4 = Infrared Proximity Sensor
  J5 = Infrared Proximity Sensor
  J6 = Basic Servo
  Load_Cell1 = Load Cell - Red/white/black/green
  Part2 = HX711 Weighing Sensor Module
  Raspberry_Pi_4 = Raspberry Pi 3 [part_number=RPI-3-V1.2]  # not connected
  7"_capacitive_LCD = Arduino Color LCD Shield  # not connected
  U1 = Sharp PC817 [part_number=PC817XI package=SMT]
  U2 = Sharp PC817 [part_number=PC817XI package=SMT]
  U3 = Sharp PC817 [part_number=PC817XI package=SMT]
  U4 = Sharp PC817 [part_number=PC817XI package=SMT]
  V1 = DC Power [voltage=6]
  R1 = Resistor [tolerance=±5% resistance=2.2k package="2010 [SMD]"]
  R2 = Resistor [tolerance=±5% resistance=2.2k package="2010 [SMD]"]
  R3 = Resistor [tolerance=±5% resistance=2.2k package="2010 [SMD]"]
  R4 = Resistor [tolerance=±5% resistance=2.2k package="2010 [SMD]"]
  R5 = Resistor [tolerance=±5% resistance=10k package="2010 [SMD]"]
  R6 = Resistor [tolerance=±5% resistance=10k package="2010 [SMD]"]
  R7 = Resistor [tolerance=±5% resistance=10k package="2010 [SMD]"]
  R8 = Resistor [tolerance=±5% resistance=10k package="2010 [SMD]"]
  V2 = DC Power [voltage=5]
  V3 = DC Power [voltage=7.4]

nets:
  N1: Part1.D13_PWM, U3.Pin_4, R6.Pin_0
  N2: Part1.D12_PWM, U2.Pin_4, R5.Pin_0
  N3: Part1.D11_PWM, U1.Pin_4, R7.Pin_1
  N4: Part1.D10_PWM, U4.Pin_4, R8.Pin_0
  N5: Part1.D2_PWM, Part2.CK/TX
  N6: Part1.D3_PWM, Part2.DO/RX
  N7: Part1.D5_PWM, J1.pulse
  N8: Part1.D6_PWM, J6.pulse
  5V: Part1.5V, Part2.VCC
  GND: J1.gnd, J6.gnd
  N9: J1.vcc, V3.V+
  N10: J2.Vout, R1.Pin_1
  GND_2: J2.GND, J3.GND, J4.GND, J5.GND, U1.Pin_2, U2.Pin_2, U3.Pin_2, U4.Pin_2, V1.V-
  VCC: J2.Vcc, J3.Vcc, J4.Vcc, J5.Vcc, V1.V+
  N11: J3.Vout, R2.Pin_1
  N12: J4.Vout, R4.Pin_1
  N13: J5.Vout, R3.Pin_1
  N14: Load_Cell1.wire1, Part2.E+
  N15: Load_Cell1.wire2, Part2.A-
  N16: Load_Cell1.wire3, Part2.E-
  N17: Load_Cell1.wire4, Part2.A+
  N18: U1.Pin_1, R3.Pin_0
  GND_3: U1.Pin_3, U2.Pin_3, U4.Pin_3, V2.V-, V3.V-
  N19: U2.Pin_1, R4.Pin_0
  N20: U3.Pin_1, R1.Pin_0
  N21: U4.Pin_1, R2.Pin_0
  N22: R6.Pin_1, R7.Pin_0, R8.Pin_1, V2.V+

custom parts:
  Load Cell - Red/white/black/green: A rectangle load cell/weighting pressure Sensor with four wires - Red, white, black, green. Normally corresponding with E+, E-, A+, A- respectively.
